# Fritzing sketch bookshelf (saved by Fritzing 0.9.3b)
breadboards: 1

parts:
  부품1 = Arduino Uno (Rev3)
  hc-sr1 = hc-sr04
  hc-sr2 = hc-sr04
  IC1 = SHIFT REGISTER [package=dil16]
  R1 = Resistor [tolerance=±5% resistance=220 package=THT]
  R2 = Resistor [tolerance=±5% resistance=220 package=THT]
  R3 = Resistor [tolerance=±5% resistance=220 package=THT]
  R4 = Resistor [tolerance=±5% resistance=220 package=THT]
  R5 = Resistor [tolerance=±5% resistance=220 package=THT]
  R6 = Resistor [tolerance=±5% resistance=220 package=THT]
  R7 = Resistor [tolerance=±5% resistance=220 package=THT]
  R8 = Resistor [tolerance=±5% resistance=220 package=THT]
  LED1 = LED - 5mm [color="Red (633nm)" package="5 mm [THT]"]
  LED2 = LED - 5mm [color="Red (633nm)" package="5 mm [THT]"]
  LED3 = LED - 5mm [color="Red (633nm)" package="5 mm [THT]"]
  LED4 = LED - 5mm [color="Red (633nm)" package="5 mm [THT]"]
  LED5 = LED - 5mm [color="Red (633nm)" package="5 mm [THT]"]
  LED6 = LED - 5mm [color="Red (633nm)" package="5 mm [THT]"]
  LED7 = LED - 5mm [color="Red (633nm)" package="5 mm [THT]"]
  LED8 = LED - 5mm [color="Red (633nm)" package="5 mm [THT]"]

nets:
  N1: 부품1.D8, IC1.SCK
  N2: 부품1.D9_PWM, IC1.SER
  N3: 부품1.D10_PWM/SS, IC1.RCK
  N4: 부품1.D3_PWM, hc-sr2.Echo
  N5: 부품1.D4, hc-sr2.Trig
  N6: 부품1.D6_PWM, hc-sr1.Echo
  N7: 부품1.D7, hc-sr1.Trig
  VCC: 부품1.5V, hc-sr1.VCC, hc-sr2.VCC, IC1.SCL, IC1.VCC
  GND: hc-sr1.GND, hc-sr2.GND, IC1.GND, IC1.G, LED1.cathode, LED2.cathode, LED3.cathode, LED4.cathode, LED5.cathode, LED6.cathode, LED7.cathode, LED8.cathode
  N8: IC1.QB, R1.Pin_1
  N9: IC1.QC, R2.Pin_1
  N10: IC1.QD, R4.Pin_1
  N11: IC1.QE, R8.Pin_0
  N12: IC1.QF, R7.Pin_0
  N13: IC1.QG, R6.Pin_0
  N14: IC1.QH, R5.Pin_0
  N15: IC1.QA, R3.Pin_1
  N16: R1.Pin_0, LED6.anode
  N17: R2.Pin_0, LED7.anode
  N18: R3.Pin_0, LED5.anode
  N19: R4.Pin_0, LED8.anode
  N20: R5.Pin_1, LED1.anode
  N21: R6.Pin_1, LED2.anode
  N22: R7.Pin_1, LED3.anode
  N23: R8.Pin_1, LED4.anode
